# Fritzing sketch blackbox (saved by Fritzing 0.6.3b)
breadboards: 1

parts:
  Blue_SMiRF_Silver1 = BlueSMiRF Silver
  U1 = 3-Axis Accelerometer Breakout
  Arduino1 = Arduino
  J1 = Infrared Proximity Sensor

nets:
  N1: Blue_SMiRF_Silver1.RTS, Blue_SMiRF_Silver1.CTS
  N2: Blue_SMiRF_Silver1.RX, Arduino1.D1TX
  N3: Blue_SMiRF_Silver1.TX, Arduino1.D0RX
  N4: U1.Z, Arduino1.D4
  N5: U1.Y, Arduino1.D3
  N6: U1.X, Arduino1.D2
  GND: U1.GND, Arduino1.GND, J1.GND
  VDD: U1.VDD, Arduino1.+5V, J1.Vcc
  N7: Arduino1.A0, J1.Vout

custom parts:
  BlueSMiRF Silver: Small and conviently packaged bluetooth serial radio modem
